// Logisim project cpu.circ as structural Verilog: 4 circuits, main circuit main
module main (
);

  wire ALU_ADD_SUB, and_1_out, BRANCH, CLK, d_ff_1_q, JMP, not_1_out, PC_SEL, RAM_READ, RAM_WRITE, REG_WRITE,
       ZERO_FLAG;
  wire [1:0] REG_ADDR, WM_SEL;
  wire [3:0] OPCODE;
  wire [7:0] alu_1_alu_out, IMM, PC_NEXT, PC_out, PC_PLUS_1, R3_UP, R_SRC, REG_OUT, W_MUX;
  wire [9:8] ROM_OUT;

  Clock clock_1 (.out(CLK));
  Register PC (.D(PC_NEXT), .clk(CLK), .Q(PC_out));  // open: en, clr
  ROM #(.dataWidth(16)) rom_1 (.addr(PC_out), .data({OPCODE, REG_ADDR, ROM_OUT, IMM}));
  Adder adder_1 (.a(PC_out), .b(8'h1), .out(PC_PLUS_1));  // open: cin, cout
  Multiplexer #(.width(8)) multiplexer_1 (.in0(PC_PLUS_1), .in1(IMM), .out(PC_NEXT), .sel(PC_SEL));
  D_Flip_Flop d_ff_1 (.clk(CLK), .D(ZERO_FLAG), .Q(d_ff_1_q));  // open: Qn, preset, reset
  ALU alu_1 (.ALU_A(REG_OUT), .ALU_B(IMM), .ALU_SRC(ALU_ADD_SUB), .ALU_OUT(alu_1_alu_out), .ZERO_FLAG(ZERO_FLAG));
  not not_1 (not_1_out, d_ff_1_q);
  RAM #(.trigger("falling")) ram_1 (
    .addr(R3_UP), .we(RAM_WRITE), .oe(RAM_READ), .clk(CLK), .din(REG_OUT), .dout(R_SRC));
  and and_1 (and_1_out, not_1_out, BRANCH);
  or or_1 (PC_SEL, and_1_out, JMP);
  // Probe on R_SRC
  Multiplexer #(.select(2), .width(8)) multiplexer_2 (
    .in0(alu_1_alu_out), .in1(R_SRC), .in2(IMM), .out(W_MUX), .sel(WM_SEL));  // open: in3
  Control_Unit control_unit_1 (
    .OPCODE(OPCODE), .REG_WRITE(REG_WRITE), .IMM_WRITE(WM_SEL[1]), .REG_DATA(WM_SEL[0]),
    .RAM_WRITE(RAM_WRITE), .RAM_READ(RAM_READ), .ALU_ADD_SUB(ALU_ADD_SUB), .BRANCH(BRANCH), .JMP(JMP));
  Register_File register_file_1 (
    .REG_WRITE_DATA(W_MUX), .CLK(CLK), .REG_WRITE(REG_WRITE), .ADDR_WRITE(REG_ADDR), .REG_READ(REG_ADDR),
    .REG_OUT(REG_OUT), .R3_UP(R3_UP));
  // Probe on R3_UP

  // Other names for the same wires on the sheet: ROM_OUT (some bits) = {OPCODE, REG_ADDR, IMM}

  // Notes on the sheet:
  //   contents of rom_1 (hex, n*v repeats v):
  //   c00 1400 800 3c01 1000 4c01 2000 3801 3c01 5809 6003 2400 7000
endmodule

module Register_File (
  input  [7:0] REG_WRITE_DATA,
  input  CLK,
  input  REG_WRITE,
  input  [1:0] ADDR_WRITE,
  input  [1:0] REG_READ,
  output [7:0] REG_OUT,
  output [7:0] R3_UP
);

  wire decoder_1_out0, decoder_1_out1, decoder_1_out2, decoder_1_out3;
  wire [7:0] R0_OUT, R1_OUT, R2_OUT;

  Decoder #(.select(2)) decoder_1 (
    .out0(decoder_1_out0), .out1(decoder_1_out1), .out2(decoder_1_out2), .out3(decoder_1_out3),
    .sel(ADDR_WRITE), .en(REG_WRITE));
  Register R0 (.D(REG_WRITE_DATA), .en(decoder_1_out0), .clk(CLK), .Q(R0_OUT));  // open: clr
  Register R1 (.D(REG_WRITE_DATA), .en(decoder_1_out1), .clk(CLK), .Q(R1_OUT));  // open: clr
  Register R2 (.D(REG_WRITE_DATA), .en(decoder_1_out2), .clk(CLK), .Q(R2_OUT));  // open: clr
  Register R3 (.D(REG_WRITE_DATA), .en(decoder_1_out3), .clk(CLK), .Q(R3_UP));  // open: clr
  Multiplexer #(.select(2), .width(8)) multiplexer_1 (
    .in0(R0_OUT), .in1(R1_OUT), .in2(R2_OUT), .in3(R3_UP), .out(REG_OUT), .sel(REG_READ));

  // Other names for the same wires on the sheet: R3_OUT[7:0] = R3_UP
endmodule

module Control_Unit (
  input  [3:0] OPCODE,
  output REG_WRITE,
  output IMM_WRITE,
  output REG_DATA,
  output RAM_WRITE,
  output RAM_READ,
  output ALU_ADD_SUB,
  output BRANCH,
  output JMP
);

  ROM #(.addrWidth(4)) IR_STR (
    .addr(OPCODE), .data({JMP, BRANCH, ALU_ADD_SUB, RAM_READ, RAM_WRITE, REG_DATA, IMM_WRITE, REG_WRITE}));

  // Other names for the same wires on the sheet: IR[7:0] = {JMP, BRANCH, ALU_ADD_SUB, RAM_READ, RAM_WRITE, REG_DATA, IMM_WRITE, REG_WRITE}

  // Notes on the sheet:
  //   contents of IR_STR (hex, n*v repeats v):
  //   3 15 8 1 21 20 40 80
endmodule

module ALU (
  input  [7:0] ALU_A,
  input  [7:0] ALU_B,
  input  ALU_SRC,
  output [7:0] ALU_OUT,
  output ZERO_FLAG
);

  wire [7:0] adder_1_out, SUB;

  Adder adder_1 (.a(ALU_A), .b(ALU_B), .out(adder_1_out));  // open: cin, cout
  Subtractor subtractor_1 (.a(ALU_A), .b(ALU_B), .out(SUB));  // open: bin, bout
  nor nor_1 (ZERO_FLAG, SUB[0], SUB[1], SUB[2], SUB[3], SUB[4], SUB[5], SUB[6], SUB[7]);
  Multiplexer #(.width(8)) multiplexer_1 (.in0(adder_1_out), .in1(SUB), .out(ALU_OUT), .sel(ALU_SRC));
endmodule
